# Fritzing sketch FullDiagram (saved by Fritzing 0.9.3b)

parts:
  Arduino_Uno_+_MP3_Shield = Arduino MP3 Player Shield
  Part2 = Arduino Uno (Rev3) - ICSP  # not connected
  Power_Supply_(3_7V) = Battery Holders [package=lipo-1100mAh]
  Servo = Basic Servo
  Boost_Converter_(3_7V->5V) = RioRand LM2596
  U1 = SWITCH_SPDT [package=kps-1290]
  Li-Po_Charger = TP4056 Charger
  IR_Distance_Sensor_(Connected_to_Servo) = Infrared Proximity Sensor

nets:
  N1: Arduino_Uno_+_MP3_Shield.A0, IR_Distance_Sensor_(Connected_to_Servo).Vout
  N2: Arduino_Uno_+_MP3_Shield.5V-MIDI-RX, Servo.pulse
  GND: Arduino_Uno_+_MP3_Shield.GND, Boost_Converter_(3_7V->5V).Pin_4, IR_Distance_Sensor_(Connected_to_Servo).GND
  VIN: Arduino_Uno_+_MP3_Shield.VIN, Servo.vcc, Boost_Converter_(3_7V->5V).Pin_3
  N3: Power_Supply_(3_7V).+, U1.P
  N4: Power_Supply_(3_7V).-, Boost_Converter_(3_7V->5V).Pin_2, Li-Po_Charger.IN-, Li-Po_Charger.BAT-
  N5: Boost_Converter_(3_7V->5V).Pin_1, U1.S, Li-Po_Charger.IN+, Li-Po_Charger.BAT+
